# Fritzing sketch Alarme (saved by Fritzing 0.9.3b)
breadboards: 1

parts:
  Composant1 = Arduino Uno (Rev3)
  LED1 = LED - 5mm [color="Red (633nm)" package="5 mm [THT]"]
  SPKR1 = Loudspeaker
  S1 = Reed switch [package=THT]
  S2 = Tilt Switch [package=THT]

nets:
  N1: Composant1.GND, LED1.cathode, SPKR1.pin1, S1.pin_1
  N2: Composant1.D2, LED1.anode, SPKR1.pin2
  N3: Composant1.D3_PWM, S2.Pin_2
  N4: S1.pin_2, S2.Pin_1
